# Fritzing sketch Leave_the_room_ESP_Schematic (saved by Fritzing 0.8.7b)
breadboards: 1

parts:
  U2 = NodeMCU V1.0
  Part1 = Arduino Uno (Rev3) - ICSP
  Part2 = SRF05 Ultrasonic Rangefinder
  R1 = Resistor [tolerance=±5% resistance=220 package=THT]
  LED1 = LED - 5mm [color="Red (633nm)" package="5 mm [THT]"]
  S1 = Pushbutton [package="[THT]"]
  R2 = Photocell (LDR) [package=THT]
  R3 = Resistor [tolerance=±5% resistance=10k package=THT]

nets:
  N1: U2.D2, R1.Pin_1
  N2: U2.D4, S1.Pin_3, S1.Pin_4
  N3: U2.3V3, R2.pin_0
  GND: U2.GND, Part1.GND, Part2.GND, LED1.cathode, S1.Pin_1, S1.Pin_2, R3.Pin_1
  N4: U2.D5, Part2.Trig
  N5: U2.D7, Part2.Echo
  N6: U2.A0, R2.pin_1, R3.Pin_0
  5V: Part1.5V, Part2.VCC
  N7: R1.Pin_0, LED1.anode

custom parts:
  NodeMCU V1.0: ESP8266 based NodeMCU
