# Fritzing sketch Fridge_Schematic (saved by Fritzing 0.8.7b)
breadboards: 1

parts:
  U2 = NodeMCU V1.0
  R1 = Resistor [tolerance=±5% resistance=220 package=THT]
  LED1 = LED - 5mm [color="Red (633nm)" package="5 mm [THT]"]
  Mod1 = KY-003 Hall Magnetic Sensor Module [package="Breakout board"]
  J1 = Piezo Speaker

nets:
  N1: U2.D2, R1.Pin_1
  3V3: U2.3V3, Mod1.Vin
  N2: U2.GND, LED1.cathode, Mod1.-, J1.pin1
  N3: U2.D5, J1.pin2
  N4: U2.D6, Mod1.S
  N5: R1.Pin_0, LED1.anode

notes:
  buzzer
  magnet sensor
  LED,
  220ohm resistor

custom parts:
  NodeMCU V1.0: ESP8266 based NodeMCU
  KY-003 Hall Magnetic Sensor Module: KEYES KY-003 Arduino Hall Magnetic Sensor Module is a switch that will turn on/off in the presence of a magnetic field.
