# Fritzing sketch Leave_the_room_for_ESP (saved by Fritzing 0.9.3b)
breadboards: 1

parts:
  Part1 = Arduino Mega 2560 (Rev3)
  S2 = Pushbutton [package="[THT]"]
  HC-SR04_Sensor_1 = HC-SR04 Ultrasonic Distance Sensor
  LED1 = LED - 5mm [color="Red (633nm)" package="5 mm [THT]"]
  R1 = Resistor [tolerance=±5% resistance=220 package=THT]
  R2 = Photocell (LDR) [package=THT]
  R3 = Resistor [tolerance=±5% resistance=10k package=THT]
  U1 = NodeMCU V1.0

nets:
  5V: Part1.5V, HC-SR04_Sensor_1.VCC, R2.pin_0
  N1: S2.Pin_1, S2.Pin_2, U1.D2
  GND: S2.Pin_3, S2.Pin_4, HC-SR04_Sensor_1.GND, R1.Pin_0, R3.Pin_1, U1.GND
  N2: HC-SR04_Sensor_1.TRIG, U1.D3
  N3: HC-SR04_Sensor_1.ECHO, U1.D4
  N4: LED1.cathode, U1.D5
  N5: LED1.anode, R1.Pin_1
  N6: R2.pin_1, R3.Pin_0, U1.A0

custom parts:
  NodeMCU V1.0: ESP8266 based NodeMCU
