# Fritzing sketch frtizingLeaveHouse (saved by Fritzing 0.9.3b)
breadboards: 1

parts:
  U2 = NodeMCU V1.0
  SM1 = 28BYJ-48 Stepper Motor [part_number=28BYJ-48]  # not connected
  Driver1 = 28BYJ-48 Driver Module [part_number=ULN2003 package=THT]
  LED1 = RGB LED (com. cathode, rgb) [package="5 mm [THT]"]
  Componente1 = Arduino Uno (Rev3)

nets:
  N1: U2.D1, LED1.red_anode
  N2: U2.D2, LED1.green_anode
  N3: U2.D3, LED1.blue_anode
  GND: U2.GND, Driver1.GND, LED1.common_cathode
  N4: U2.D5, Driver1.IN1
  N5: U2.D6, Driver1.IN2
  N6: U2.D7, Driver1.IN3
  N7: U2.D8, Driver1.IN4
  N8: Driver1.Vmotor, Componente1.5V

custom parts:
  NodeMCU V1.0: ESP8266 based NodeMCU
  28BYJ-48 Stepper Motor: Unipolar Stepper Motor 28BYJ-48 Top coil - pink & orange Bottom coil - blue & yellow Common rail - red Connector pins: blue - pink - yellow - orange - red
  28BYJ-48 Driver Module: ULN2003 Driver Module for the 28BYJ-48 Unipolar Stepper Motor LED A - Blue wire - Bottom coil left LED B - Pink wire - Top coil left LED C - Yellow wire - Bottom coil right LED D - Orange wire - Top coil right Common rail - red Connector pins: blue - pink - yellow - orange - red Control pins - IN1 to IN4 Power pins - GND & Vmotor (5-12V) On/Off jumper (if removed, power to motor is cut).
