# Fritzing sketch temp_rgbled (saved by Fritzing 0.9.3b)
breadboards: 1

parts:
  R1 = Resistor [tolerance=±5% resistance=220 package=THT]
  R2 = Resistor [tolerance=±5% resistance=220 package=THT]
  R3 = Resistor [tolerance=±5% resistance=220 package=THT]
  T1 = LM35 Temperature Sensor [package="TO92 [THT]"]
  Componente1 = Arduino Uno (Rev3)
  LED1 = RGB LED (com. cathode, rgb) [package="5 mm [THT]"]

nets:
  N1: R1.Pin_0, Componente1.D13/SCK
  N2: R1.Pin_1, LED1.red_anode
  N3: R2.Pin_0, Componente1.D12/MISO
  N4: R2.Pin_1, LED1.green_anode
  N5: R3.Pin_0, Componente1.D11_PWM/MOSI
  N6: R3.Pin_1, LED1.blue_anode
  N7: T1.+Vs, Componente1.5V
  N8: T1.Vout, Componente1.A0
  GND: T1.GND, Componente1.GND, LED1.common_cathode
